// Logisim project Datapath.circ as structural Verilog: 1 circuit, main circuit datapath
module datapath (
);

  wire clock_1_out, main_1_p1, main_1_p4, main_1_p6, undriven, undriven_2, undriven_4, undriven_5;
  wire [4:0] decoder_1_rd, decoder_1_rs, decoder_1_rt, decoder_1_shamt, multiplexer_1_out, multiplexer_2_out;
  wire [5:0] decoder_1_funct, decoder_1_opcode;
  wire [15:0] decoder_1_imm;
  wire [31:0] datamem_1_dados_lidos, main_1_p5, meminstr_1_instruction, multiplexer_3_out,
       registerfile_1_ld1, registerfile_1_ld2, undriven_3;

  Clock clock_1 (.out(clock_1_out));
  MemInstr meminstr_1 (.Instruction(meminstr_1_instruction));  // open: PC_address
  Decoder decoder_1 (
    .INST(meminstr_1_instruction), .FUNCT(decoder_1_funct), .SHAMT(decoder_1_shamt), .IMM(decoder_1_imm),
    .RD(decoder_1_rd), .RT(decoder_1_rt), .RS(decoder_1_rs), .Opcode(decoder_1_opcode));  // open: ADDR
  Multiplexer #(.width(5), .enable("false")) multiplexer_1 (
    .in0(decoder_1_rt), .in1(decoder_1_rd), .out(multiplexer_1_out), .sel(undriven));
  // ControllerUnity controllerunity_1: pin names not known; wires that end beside it: decoder_1_opcode
  RegisterFile registerfile_1 (
    .LR1(decoder_1_rs), .WD(undriven_3), .RegWrite(undriven_4), .LR2(decoder_1_rt), .WR(multiplexer_2_out),
    .LD1(registerfile_1_ld1), .LD2(registerfile_1_ld2), .Clock(clock_1_out));
  Multiplexer #(.width(5), .enable("false")) multiplexer_2 (
    .in0(multiplexer_1_out), .in1({5{1'b1}}), .out(multiplexer_2_out), .sel(undriven_2));
  Extensor extensor_1 (.in_1(decoder_1_imm));  // open: out_2
  ULAControllerUnity ulacontrollerunity_1 (.Funct(decoder_1_funct));  // open: Op, ALUOp
  Multiplexer #(.width(32), .enable("false")) multiplexer_3 (
    .in0(registerfile_1_ld2), .out(multiplexer_3_out), .sel(main_1_p1));  // open: in1
  // ULA_main main_1: pin names not known; wires that end beside it: main_1_p1, registerfile_1_ld1, multiplexer_3_out, main_1_p4, main_1_p5, main_1_p6, decoder_1_shamt
  datamem datamem_1 (
    .Escreve_dado(registerfile_1_ld2), .Dados_lidos(datamem_1_dados_lidos), .MemRead(undriven_5),
    .clk(clock_1_out));  // open: Endereço, MemWrite, clear
  Multiplexer #(.width(32), .enable("false")) multiplexer_4 (
    .in0(main_1_p5), .in1(datamem_1_dados_lidos));  // open: out, sel
endmodule
