// Logisim project MemoryInst.circ as structural Verilog: 1 circuit, main circuit MemInstr
module MemInstr (
  input  [31:0] PC_address,
  output [31:0] Instruction
);

  ROM #(.addrWidth(24), .dataWidth(32), .Select("high")) rom_1 (.addr(PC_address[25:2]), .data(Instruction));
endmodule
